# Fritzing sketch Test Bot Controller (saved by Fritzing 0.9.10b)

parts:
  Arduino_Mega = Arduino Mega 2560 (Rev3)
  Joystick = Thumb Joystick
  Radio = NRF24L01+ Breakout Board
  C1 = Electrolytic Capacitor [capacitance=10µF voltage=35V package="100 mil [THT, electrolytic]"]

nets:
  N1: Arduino_Mega.A0, Joystick.VERT
  N2: Arduino_Mega.A1, Joystick.HORZ
  N3: Arduino_Mega.A2, Joystick.SEL
  N4: Arduino_Mega.D8_PWM, Radio.CS
  VCC: Arduino_Mega.5V, Joystick.VCC, Radio.VCC, C1.+
  GND: Arduino_Mega.GND, Joystick.GND, Radio.GND, C1.-
  N5: Arduino_Mega.D7_PWM, Radio.CE
  N6: Arduino_Mega.D50, Radio.MOSI
  N7: Arduino_Mega.D51, Radio.MISO
  N8: Arduino_Mega.D52, Radio.SCK
