# Fritzing sketch Test Bot (saved by Fritzing 0.9.10b)
stripboards: 2

parts:
  Part1 = Arduino Uno (Rev3)
  Part2 = NRF24L01+ Breakout Board
  IC1 = L293D [package=THT]
  M1 = gear-motor
  M2 = gear-motor
  C1 = Electrolytic Capacitor [capacitance=1µF voltage=35V package="100 mil [THT, electrolytic]"]
  VCC3 = Battery block 9V

nets:
  N1: Part1.D8, Part2.CS
  N2: Part1.D9_PWM, IC1.In_2
  N3: Part1.D11_PWM/MOSI, Part2.MOSI
  N4: Part1.D12/MISO, Part2.MISO
  N5: Part1.D13/SCK, Part2.SCK
  N6: Part1.D2, IC1.Enable_1
  N7: Part1.D3_PWM, IC1.In_4
  N8: Part1.D4, IC1.Enable_2
  N9: Part1.D5_PWM, IC1.In_3
  N10: Part1.D6_PWM, IC1.In_1
  N11: Part1.D7, Part2.CE
  5V: Part1.5V, Part2.VCC, IC1.+V, C1.+
  GND: Part1.GND, Part2.GND, IC1.0V, C1.-, VCC3.-
  N12: IC1.Out_1_(_Controlled_by_Enable_1_), M2.pin_1
  N13: IC1.Out_2_(_Controlled_by_Enable_1_), M2.pin_2
  N14: IC1.+Vmotor, VCC3.+
  N15: IC1.Out_3_(_Controlled_by_Enable_2_), M1.pin_1
  N16: IC1.Out_4_(_Controlled_by_Enable_2_), M1.pin_2
