# Fritzing sketch Transceiver Circuit High Power (saved by Fritzing 0.9.10b)

parts:
  Part1 = Arduino Pro Mini v13
  ML01DP5_1 = NRF24L01+ Breakout Board
  R1 = Resistor [tolerance=±5% power=0.25 resistance=220 package=THT]
  LED1 = LED - 5mm [color="Red (633nm)" current=0.030 package="5 mm [THT]"]
  C1 = Electrolytic Capacitor [capacitance=10µF voltage=35V package="100 mil [THT, electrolytic]"]
  VCC1 = Battery block 9V
  Part2 = Arduino Pro Mini v13
  ML01DP5_2 = NRF24L01+ Breakout Board
  C2 = Electrolytic Capacitor [capacitance=10µF voltage=35V package="100 mil [THT, electrolytic]"]
  VCC2 = Battery block 9V
  S1 = Pushbutton [package="[THT]"]
  R2 = Resistor [tolerance=±5% power=0.25 resistance=10k package=THT]

nets:
  N1: Part1.RAW, VCC1.+
  GND: Part1.GND, ML01DP5_1.GND, LED1.cathode, C1.-, VCC1.-
  VCC: Part1.VCC, ML01DP5_1.VCC, C1.+
  N2: Part1.D13/SCK, ML01DP5_1.SCK
  N3: Part1.D12/MISO, ML01DP5_1.MISO
  N4: Part1.D11_PWM/MOSI, ML01DP5_1.MOSI
  N5: Part1.D8, ML01DP5_1.CE
  N6: Part1.D7, ML01DP5_1.CS
  N7: Part1.D6_PWM, R1.Pin_0
  N8: R1.Pin_1, LED1.anode
  N9: Part2.VCC, VCC2.-, S1.Pin_1, S1.Pin_2, R2.Pin_1
  GND_2: Part2.GND, ML01DP5_2.GND, C2.-
  N10: Part2.RAW, VCC2.+
  N11: Part2.D13/SCK, ML01DP5_2.SCK
  N12: Part2.D12/MISO, ML01DP5_2.MISO
  N13: Part2.D11_PWM/MOSI, ML01DP5_2.MOSI
  N14: Part2.D8, ML01DP5_2.CE
  N15: Part2.D7, ML01DP5_2.CS
  N16: Part2.D6_PWM, S1.Pin_3, S1.Pin_4, R2.Pin_0
  N17: ML01DP5_2.VCC, C2.+
