# Fritzing sketch Transceiver Test Circuit (saved by Fritzing 0.9.10b)

parts:
  Part1 = Arduino Pro Mini (3.3V)
  Part2 = NRF24L01+ Breakout Board
  Part3 = Arduino Pro Mini (3.3V)
  Part4 = NRF24L01+ Breakout Board
  LED1 = LED - 5mm [color="Red (633nm)" current=0.030 package="5 mm [THT]"]
  S1 = Pushbutton [package="[THT]"]
  R2 = Resistor [tolerance=±5% power=0.25 resistance=10k package=THT]
  R3 = Resistor [tolerance=±5% power=0.25 resistance=220 package=THT]
  C1 = Electrolytic Capacitor [capacitance=10µF voltage=35V package="100 mil [THT, electrolytic]"]
  C2 = Electrolytic Capacitor [capacitance=10µF voltage=35V package="100 mil [THT, electrolytic]"]
  VCC1 = Battery block 9V
  VCC2 = Battery block 9V

nets:
  GND: Part1.GND, Part2.GND, LED1.cathode, C1.-, VCC2.-
  N1: Part1.RAW, VCC2.+
  VCC: Part1.VCC, Part2.VCC, C1.+
  N2: Part1.SCK, Part2.SCK
  N3: Part1.MISO, Part2.MISO
  N4: Part1.MOSI, Part2.MOSI
  N5: Part1.D8, Part2.CE
  N6: Part1.D7, Part2.CS
  N7: Part1.D6, R3.Pin_0
  GND_2: Part3.GND, Part4.GND, R2.Pin_0, C2.-, VCC1.-
  N8: Part3.RAW, VCC1.+
  VCC_2: Part3.VCC, Part4.VCC, S1.Pin_1, C2.+
  N9: Part3.SCK, Part4.SCK
  N10: Part3.MISO, Part4.MISO
  N11: Part3.MOSI, Part4.MOSI
  N12: Part3.D8, Part4.CE
  N13: Part3.D7, Part4.CS
  N14: Part3.D6, S1.Pin_4, R2.Pin_1
  N15: LED1.anode, R3.Pin_1
